// Logisim project IE4756-fast-adder.circ as structural Verilog: 4 circuits, main circuit main
module cla4 (
  input  [3:0] in_1,
  input  [3:0] in_2,
  input  in_3,
  output [3:0] out_4,
  output out_5,
  output out_6,
  output out_7
);

  wire and_1_p2, and_2_p2, and_3_p2, and_4_p2, and_5_out, and_7_out, and_8_out, and_9_out, and_10_out,
       and_11_out, and_12_out, and_13_out, and_14_out, and_15_out, or_1_p1, or_2_out, or_3_out, or_4_out,
       undriven, undriven_2, undriven_3, undriven_4, undriven_5, undriven_6, undriven_7, undriven_8,
       undriven_9, undriven_10, undriven_11, undriven_12, undriven_13, undriven_14, undriven_15, undriven_16,
       undriven_17, undriven_18, undriven_19, undriven_20, undriven_21, xor_1_p2, xor_1_p3, xor_2_p2,
       xor_2_p3, xor_3_p2, xor_3_p3, xor_4_p2, xor_4_p3;

  // AND_Gate and_1: pin names not known; wires that end beside it: in_2[3], and_1_p2
  // AND_Gate and_2: pin names not known; wires that end beside it: in_2[2], and_2_p2
  // AND_Gate and_3: pin names not known; wires that end beside it: in_2[1], and_3_p2
  // AND_Gate and_4: pin names not known; wires that end beside it: in_2[0], and_4_p2
  // XOR_Gate #(.\xor ("odd")) xor_1: pin names not known; wires that end beside it: in_1[3], xor_1_p2, xor_1_p3
  // XOR_Gate #(.\xor ("odd")) xor_2: pin names not known; wires that end beside it: in_1[2], xor_2_p2, xor_2_p3
  // XOR_Gate #(.\xor ("odd")) xor_3: pin names not known; wires that end beside it: in_1[1], xor_3_p2, xor_3_p3
  // XOR_Gate #(.\xor ("odd")) xor_4: pin names not known; wires that end beside it: in_1[0], xor_4_p2, xor_4_p3
  buf xor_5 (out_4[3], xor_1_p2);  // XOR_Gate
  buf xor_6 (out_4[2], xor_2_p2);  // XOR_Gate
  buf xor_7 (out_4[1], xor_3_p2);  // XOR_Gate
  buf xor_8 (out_4[0], xor_4_p2);  // XOR_Gate
  and and_5 (and_5_out, undriven_5, undriven_19);
  and and_6 (and_5_out, undriven_6, undriven_20);
  and and_7 (and_7_out, undriven_9, undriven_2);
  buf and_8 (and_8_out, undriven_7);  // AND_Gate
  and and_9 (and_9_out, undriven_14, undriven_3);
  buf and_10 (and_10_out, undriven_10);  // AND_Gate
  and and_11 (and_11_out, undriven_11, undriven_8);
  and and_12 (and_12_out, undriven_18, undriven_4);
  buf and_13 (and_13_out, undriven_15);  // AND_Gate
  and and_14 (and_14_out, undriven_16, undriven_12);
  and and_15 (and_15_out, out_7, undriven_21);
  // OR_Gate or_1: pin names not known; wires that end beside it: or_1_p1, and_5_out
  or or_2 (or_2_out, undriven, and_5_out);
  and and_16 (out_7, undriven_13, undriven_17);
  or or_3 (or_3_out, and_7_out, and_7_out);
  or or_4 (or_4_out, and_9_out, and_10_out);
  or or_5 (out_6, and_12_out, and_13_out);
  or or_6 (out_5, out_6, and_15_out);
endmodule

module cla32 (
  input  [31:0] in_1,
  input  [31:0] in_2,
  input  in_3,
  output [31:0] out_4,
  output out_5
);

  wire and_2_out, and_3_p1, and_3_p2, and_3_p3, and_4_out, and_5_p1, and_5_p2, and_5_p3, and_5_p4, and_6_out,
       and_8_out, and_9_out, and_11_out, and_13_out, and_15_out, and_20_out, and_28_out, and_32_out,
       and_35_out, cla4_1_p5, cla4_1_p6, cla4_2_p3, cla4_2_p5, cla4_2_p6, cla4_3_p3, cla4_3_p5, cla4_3_p6,
       cla4_4_p3, cla4_4_p5, cla4_4_p6, cla4_5_p3, cla4_5_p5, cla4_6_p3, cla4_6_p5, cla4_6_p6, cla4_7_p3,
       cla4_7_p5, cla4_7_p6, cla4_8_out_6, cla4_8_out_7, or_7_out, undriven, undriven_2, undriven_3,
       undriven_4, undriven_5, undriven_6, undriven_7, undriven_8, undriven_9, undriven_10, undriven_11,
       undriven_12, undriven_13, undriven_14, undriven_15, undriven_16, undriven_17, undriven_18,
       undriven_19, undriven_20, undriven_21, undriven_22, undriven_23, undriven_24, undriven_25,
       undriven_26, undriven_27, undriven_28, undriven_29, undriven_30, undriven_31, undriven_32,
       undriven_33, undriven_34, undriven_35, undriven_36, undriven_37, undriven_38, undriven_39,
       undriven_40, undriven_41, undriven_42, undriven_43, undriven_44, undriven_45, undriven_46,
       undriven_47, undriven_48, undriven_49, undriven_50, undriven_51, undriven_52, undriven_53,
       undriven_54, undriven_55, undriven_56, undriven_57, undriven_58, undriven_59, undriven_60,
       undriven_61, undriven_62, undriven_63, undriven_64, undriven_65, undriven_66, undriven_67, undriven_68;

  // cla4 cla4_1: pin names not known; wires that end beside it: in_1[31:28], in_2[31:28], in_1[31:28], {out_4[31:8], out_4[19:16], out_4[31:28]}, cla4_1_p5, cla4_1_p6
  // cla4 cla4_2: pin names not known; wires that end beside it: in_1[27:24], in_2[27:24], cla4_2_p3, out_4[27:24], cla4_2_p5, cla4_2_p6
  // cla4 cla4_3: pin names not known; wires that end beside it: in_1[23:20], in_2[23:20], cla4_3_p3, out_4[23:20], cla4_3_p5, cla4_3_p6
  // cla4 cla4_4: pin names not known; wires that end beside it: in_1[19:16], in_2[19:16], cla4_4_p3, out_4[19:16], cla4_4_p5, cla4_4_p6
  // cla4 cla4_5: pin names not known; wires that end beside it: in_1[15:12], in_2[15:12], cla4_5_p3, out_4[15:12], cla4_5_p5, cla4_3_p6
  // cla4 cla4_6: pin names not known; wires that end beside it: in_1[11:8], in_2[11:8], cla4_6_p3, out_4[11:8], cla4_6_p5, cla4_6_p6
  // cla4 cla4_7: pin names not known; wires that end beside it: in_1[7:4], in_2[7:4], cla4_7_p3, out_4[19:16], cla4_7_p5, cla4_7_p6
  cla4 cla4_8 (
    .in_1(in_1[3:0]), .in_2(in_2[3:0]), .in_3(or_7_out), .out_4(out_4[31:28]), .out_6(cla4_8_out_6),
    .out_7(cla4_8_out_7));  // open: out_5
  // AND_Gate and_1 has open pins: in0=undriven_19, in1=undriven_67, out=open
  and and_2 (and_2_out, undriven_20, undriven);
  // AND_Gate and_3: pin names not known; wires that end beside it: and_3_p1, and_3_p2, and_3_p3, and_3_p1, and_2_out
  and and_4 (and_4_out, undriven_23, undriven_6);
  // AND_Gate and_5: pin names not known; wires that end beside it: and_5_p1, and_5_p2, and_5_p3, and_5_p4
  and and_6 (and_6_out, undriven_2, undriven_27, undriven_8, undriven_28);
  and and_7 (and_6_out, undriven_27, undriven_8);
  and and_8 (and_8_out, undriven_68, undriven_24, undriven_29);
  and and_9 (and_9_out, undriven_7, cla4_3_p6, undriven_10, undriven_33);
  and and_10 (and_9_out, cla4_3_p6, undriven_10);
  and and_11 (and_11_out, undriven_33, undriven_3, undriven_30, undriven_34, undriven_9);
  and and_12 (and_11_out, undriven_3, undriven_30, undriven_34);
  and and_13 (and_13_out, undriven_9, undriven_39, undriven_12, undriven_40);
  and and_14 (and_13_out, undriven_39, undriven_12);
  and and_15 (and_15_out, undriven_40, undriven_35, undriven_36, undriven_41, undriven_11);
  and and_16 (and_15_out, undriven_35, undriven_36, undriven_41);
  and and_17 (and_15_out, undriven_41, undriven_11, undriven_50, undriven_14, undriven_51, undriven_42);
  and and_18 (and_15_out, undriven_11, undriven_50, undriven_14, undriven_51);
  and and_19 (and_15_out, undriven_50, undriven_14);
  and and_20 (and_20_out, undriven_51, undriven_42, undriven_43, undriven_52, undriven_13);
  and and_21 (and_20_out, undriven_42, undriven_43, undriven_52);
  and and_22 (and_15_out, undriven_52, undriven_13, undriven_60, undriven_17, undriven_61, undriven_53);
  and and_23 (and_15_out, undriven_13, undriven_60, undriven_17, undriven_61);
  and and_24 (and_15_out, undriven_60, undriven_17);
  and and_25 (and_15_out, undriven_17, undriven_61, undriven_53, undriven_54, undriven_62, undriven_15, undriven_55);
  and and_26 (and_15_out, undriven_61, undriven_53, undriven_54, undriven_62, undriven_15);
  and and_27 (and_15_out, undriven_53, undriven_54, undriven_62);
  and and_28 (and_28_out, undriven_62, undriven_15, undriven_55, undriven_44, undriven_56, undriven_63);
  and and_29 (and_28_out, undriven_15, undriven_55, undriven_44, undriven_56);
  and and_30 (and_15_out, undriven_44, undriven_56, undriven_63, undriven_45, undriven_57, undriven_64, undriven_46);
  and and_31 (and_15_out, undriven_56, undriven_63, undriven_45, undriven_57, undriven_64);
  and and_32 (and_32_out, undriven_45, undriven_57, undriven_64, undriven_46, undriven_65, undriven_47, undriven_58, undriven_66);
  and and_33 (and_32_out, undriven_57, undriven_64, undriven_46, undriven_65, undriven_47, undriven_58);
  and and_34 (and_28_out, undriven_65, undriven_47, undriven_58, undriven_66, undriven_48, undriven_59, undriven_37);
  and and_35 (and_35_out, undriven_66, undriven_48, undriven_59, undriven_37, undriven_31, undriven_38, undriven_25, undriven_32);
  // AND_Gate and_36 has open pins: in0=undriven_49, in1=undriven_31, in2=undriven_38, in3=undriven_25, in4=undriven_32, in5=undriven_21, in6=undriven_26, in7=undriven_4, in8=undriven_22, out=open
  // OR_Gate or_1 has open pins: out=cla4_2_p3
  or or_2 (cla4_3_p3, undriven_5, and_2_out);
  buf or_3 (cla4_4_p3, and_4_out);  // OR_Gate
  or or_4 (cla4_5_p3, and_6_out, and_8_out);
  or or_5 (cla4_6_p3, and_9_out, and_11_out, and_13_out);
  or or_6 (cla4_7_p3, and_13_out, and_15_out, and_15_out, undriven_16, and_20_out);
  or or_7 (or_7_out, and_15_out, and_20_out, and_15_out, undriven_18, and_15_out, and_15_out);
  or or_8 (out_5, and_28_out, and_15_out, and_15_out, and_28_out, and_15_out, and_32_out);
  // Pins of 1 and 4 bits meet at in_1[31:28]
  // Pins of 4 and 32 bits meet at {out_4[31:8], out_4[19:16], out_4[31:28]}

  assign in_3 = in_1[28];
  assign out_4[7:0] = {out_4[19:16], out_4[31:28]};
endmodule

module add_32 (
  input  [31:0] in_1,
  input  [31:0] in_2,
  input  in_3,
  output [31:0] out_4,
  output out_5,
  output out_6
);

  cla32 cla32_1 (.in_1(in_1), .in_2(in_2), .in_3(in_3), .out_4(out_4), .out_5(out_6));

  assign out_5 = 1'b0;
endmodule

module main (
  input  [31:0] in_1,
  input  [31:0] in_2,
  output [31:0] out_3
);

  add_32 add_32_1 (.in_1(in_1), .in_2(in_2), .out_4(out_3), .in_3(1'b0));  // open: out_5, out_6
endmodule
