// Logisim project IE4756-mips-cpu.circ as structural Verilog: 8 circuits, main circuit CPU (MIPS32)
module CPU__MIPS32 (
  input  [31:0] in_1,
  output Overflow
);

  wire and_1_out, and_2_out, and_3_out, clock_1_out, cpu_control_unit_1_branch,
       cpu_control_unit_1_branch_not_equal, cpu_control_unit_1_jump, cpu_control_unit_1_jump_register,
       cpu_control_unit_1_memory_read, cpu_control_unit_1_memory_write, cpu_control_unit_1_register_write,
       cpu_control_unit_1_signed_immediate, cpu_control_unit_1_use_md,
       cpu_control_unit_1_use_register_destination, eq_32_bit_1_p3, or_1_p3, Set_PC_out, shiftl_32_bit_1_p1,
       xor_1_out;
  wire [1:0] cpu_control_unit_1_alu_source__reg_shamt_imm, cpu_control_unit_1_md_control_bits,
       cpu_control_unit_1_move_from_low_high;
  wire [3:0] cpu_control_unit_1_alu_control_bits;
  wire [4:0] multiplexer_2_out, multiplexer_3_out, ram_1_data_3;
  wire [5:0] ram_1_data;
  wire [31:0] add_32_1_out_4, add_32_2_p4, add_32_2_p6, alu_32_bit_1_output, bit_extender_1_out,
       bit_extender_2_out, bit_extender_3_out, md_32_bit_1_output_high_bits, md_32_bit_1_output_low_bits,
       multiplexer_1_out, multiplexer_4_out, multiplexer_5_out, multiplexer_6_out, multiplexer_7_out,
       multiplexer_8_out, multiplexer_9_out, multiplexer_10_out, multiplexer_11_out,
       program_counter_interface_32_bit_1_out_5, ram_2_data, register_32_bit_1_output,
       register_32_bit_2_output, register_file_32_bit_1_output_1, register_file_32_bit_1_output_2;
  wire [31:6] ram_1_data_2;

  Clock clock_1 (.out(clock_1_out));
  Multiplexer #(.width(32), .enable("false")) multiplexer_1 (
    .in0(multiplexer_7_out), .in1(register_file_32_bit_1_output_1), .out(multiplexer_1_out),
    .sel(cpu_control_unit_1_jump_register));
  // Probe on multiplexer_1_out
  program_counter_interface__32_bit program_counter_interface_32_bit_1 (
    .Input(multiplexer_1_out), .Set_Value(in_1), .Set(Set_PC_out), .Clock(clock_1_out),
    .out_5(program_counter_interface_32_bit_1_out_5));
  Button Set_PC (.out(Set_PC_out));
  add_32 add_32_1 (
    .in_1(program_counter_interface_32_bit_1_out_5), .in_2(32'h4), .out_4(add_32_1_out_4), .in_3(1'b0));  // open: out_5, out_6
  // Probe on program_counter_interface_32_bit_1_out_5
  // Probe on ram_1_data_2[31:26]
  // Probe on ram_1_data
  // Probe on multiplexer_3_out
  // Probe on ram_1_data_3
  // Probe on ram_1_data_2[20:16]
  // Probe on multiplexer_11_out
  RAM #(.addrWidth(12), .dataWidth(32)) ram_1 (
    .addr(program_counter_interface_32_bit_1_out_5[13:2]),
    .data({ram_1_data_2[31:26], ram_1_data_3, ram_1_data_2[20:6], ram_1_data}), .clk(clock_1_out), .ld(1'b1));  // open: sel, clr
  // Probe on {ram_1_data_2[31:26], ram_1_data_3, ram_1_data_2[20:6], ram_1_data}
  CPU_control_unit cpu_control_unit_1 (
    .Opcode(ram_1_data_2[31:26]), .Funct(ram_1_data), .ALU_Control_Bits(cpu_control_unit_1_alu_control_bits),
    .MD_Control_Bits(cpu_control_unit_1_md_control_bits), .Use_MD(cpu_control_unit_1_use_md),
    .Move_From_Low_High(cpu_control_unit_1_move_from_low_high),
    .Memory_Write(cpu_control_unit_1_memory_write), .Memory_Read(cpu_control_unit_1_memory_read),
    .Jump(cpu_control_unit_1_jump), .Branch(cpu_control_unit_1_branch),
    .Branch_Not_Equal(cpu_control_unit_1_branch_not_equal),
    .ALU_Source__Reg_Shamt_Imm(cpu_control_unit_1_alu_source__reg_shamt_imm),
    .Signed_Immediate(cpu_control_unit_1_signed_immediate),
    .Register_Write(cpu_control_unit_1_register_write),
    .Use_Register_Destination(cpu_control_unit_1_use_register_destination),
    .Jump_Register(cpu_control_unit_1_jump_register));
  Multiplexer #(.width(5), .enable("false")) multiplexer_2 (
    .in0(ram_1_data_2[20:16]), .in1(ram_1_data_2[15:11]), .out(multiplexer_2_out),
    .sel(cpu_control_unit_1_use_register_destination));
  // Probe on register_file_32_bit_1_output_1
  Multiplexer #(.width(5), .enable("false")) multiplexer_3 (
    .in0(multiplexer_2_out), .in1({5{1'b1}}), .out(multiplexer_3_out), .sel(and_3_out));
  register_file__32_bit register_file_32_bit_1 (
    .Write(cpu_control_unit_1_register_write), .Write_Register(multiplexer_3_out),
    .Read_Register_1(ram_1_data_3), .Read_Register_2(ram_1_data_2[20:16]), .Input(multiplexer_11_out),
    .Clock(clock_1_out), .Output_1(register_file_32_bit_1_output_1),
    .Output_2(register_file_32_bit_1_output_2));
  assign bit_extender_1_out = {{27{1'b0}}, ram_1_data_2[10:6]};  // Bit_Extender bit_extender_1
  and and_1 (and_1_out, ram_1_data_2[15], cpu_control_unit_1_signed_immediate);
  assign bit_extender_2_out = {{6{1'b0}}, {ram_1_data_3, ram_1_data_2[20:6], ram_1_data}};  // Bit_Extender bit_extender_2
  // Probe on register_file_32_bit_1_output_2
  assign bit_extender_3_out = {{16{and_1_out}}, {ram_1_data_2[15:6], ram_1_data}};  // Bit_Extender bit_extender_3
  // Probe on multiplexer_4_out
  Multiplexer #(.width(32), .enable("false")) multiplexer_4 (
    .in0(register_file_32_bit_1_output_1), .in1(register_file_32_bit_1_output_2), .out(multiplexer_4_out),
    .sel(cpu_control_unit_1_alu_source__reg_shamt_imm[0]));
  Multiplexer #(.select(2), .width(32), .enable("false")) multiplexer_5 (
    .in0(register_file_32_bit_1_output_2), .in1(bit_extender_1_out), .in2(bit_extender_3_out),
    .in3(register_file_32_bit_1_output_1), .out(multiplexer_5_out),
    .sel(cpu_control_unit_1_alu_source__reg_shamt_imm));
  // Probe on cpu_control_unit_1_alu_source__reg_shamt_imm
  // Probe on multiplexer_5_out
  // Probe on cpu_control_unit_1_alu_control_bits
  // Probe on cpu_control_unit_1_md_control_bits
  // eq__32_bit eq_32_bit_1: pin names not known; wires that end beside it: register_file_32_bit_1_output_1, register_file_32_bit_1_output_2, eq_32_bit_1_p3
  // shiftl__32_bit shiftl_32_bit_1: pin names not known; wires that end beside it: shiftl_32_bit_1_p1
  // shiftl__32_bit shiftl_32_bit_2: pin names not known; wires that end beside it: bit_extender_3_out
  ALU__32_bit alu_32_bit_1 (
    .Control(cpu_control_unit_1_alu_control_bits), .Input_1(multiplexer_4_out), .Input_2(multiplexer_5_out),
    .Output(alu_32_bit_1_output), .Overflow(Overflow));
  MD__32_bit md_32_bit_1 (
    .Control(cpu_control_unit_1_md_control_bits), .Input_1(multiplexer_4_out), .Input_2(multiplexer_5_out),
    .Output_Low_Bits(md_32_bit_1_output_low_bits), .Output_High_Bits(md_32_bit_1_output_high_bits));
  // Probe on alu_32_bit_1_output
  and and_2 (and_2_out, cpu_control_unit_1_branch, xor_1_out);
  xor xor_1 (xor_1_out, cpu_control_unit_1_branch_not_equal, eq_32_bit_1_p3);
  // add_32 add_32_2: pin names not known; wires that end beside it: bit_extender_2_out, shiftl_32_bit_1_p1, add_32_1_out_4, add_32_2_p4, 1'b0, add_32_2_p6
  // shiftl__32_bit shiftl_32_bit_3: pin names not known
  // shiftl__32_bit shiftl_32_bit_4: pin names not known
  register__32_bit register_32_bit_1 (
    .Input(md_32_bit_1_output_low_bits), .Write(cpu_control_unit_1_use_md), .Clock(clock_1_out),
    .Output(register_32_bit_1_output));
  register__32_bit register_32_bit_2 (
    .Input(md_32_bit_1_output_high_bits), .Write(cpu_control_unit_1_use_md), .Clock(clock_1_out),
    .Output(register_32_bit_2_output));
  Multiplexer #(.width(32), .enable("false")) multiplexer_6 (
    .in0(add_32_1_out_4), .in1(add_32_2_p4), .out(multiplexer_6_out), .sel(and_2_out));
  Multiplexer #(.width(32), .enable("false")) multiplexer_7 (
    .in0(multiplexer_6_out), .in1({add_32_1_out_4[31:28], add_32_2_p6[27:0]}), .out(multiplexer_7_out),
    .sel(cpu_control_unit_1_jump));
  Multiplexer #(.width(32), .enable("false")) multiplexer_8 (
    .in0(alu_32_bit_1_output), .in1(multiplexer_9_out), .out(multiplexer_8_out),
    .sel(cpu_control_unit_1_move_from_low_high[1]));
  Multiplexer #(.width(32), .enable("false")) multiplexer_9 (
    .in0(register_32_bit_1_output), .in1(register_32_bit_2_output), .out(multiplexer_9_out),
    .sel(cpu_control_unit_1_move_from_low_high[0]));
  // OR_Gate or_1: pin names not known; wires that end beside it: cpu_control_unit_1_jump, cpu_control_unit_1_jump_register, or_1_p3
  and and_3 (and_3_out, cpu_control_unit_1_register_write, or_1_p3);
  Multiplexer #(.width(32), .enable("false")) multiplexer_10 (
    .in0(multiplexer_8_out), .in1(add_32_1_out_4), .out(multiplexer_10_out), .sel(and_3_out));
  Multiplexer #(.width(32), .enable("false")) multiplexer_11 (
    .in0(multiplexer_10_out), .in1(ram_2_data), .out(multiplexer_11_out), .sel(cpu_control_unit_1_memory_read));
  RAM #(.addrWidth(12), .dataWidth(32), .bus("separate")) ram_2 (
    .addr(alu_32_bit_1_output[13:2]), .din(register_file_32_bit_1_output_2), .data(ram_2_data),
    .str(cpu_control_unit_1_memory_write), .clk(clock_1_out), .ld(cpu_control_unit_1_memory_read));  // open: sel, clr
endmodule

module CPU_control_unit (
  input  [5:0] Opcode,
  input  [5:0] Funct,
  output [3:0] ALU_Control_Bits,
  output [1:0] MD_Control_Bits,
  output Use_MD,
  output [1:0] Move_From_Low_High,
  output Memory_Write,
  output Memory_Read,
  output Jump,
  output Branch,
  output Branch_Not_Equal,
  output [1:0] ALU_Source__Reg_Shamt_Imm,
  output Signed_Immediate,
  output Register_Write,
  output Use_Register_Destination,
  output Jump_Register
);

  wire and_1_out, and_2_out, and_3_out, and_4_out, and_5_out, and_6_out, and_7_out, and_8_out, and_9_out,
       and_10_out, and_11_out, and_12_out, and_19_out, and_20_out, and_21_out, and_22_out, and_23_out,
       and_24_out, and_26_out, and_27_out, not_1_out, not_2_out, not_3_out, not_4_out, not_5_out, not_6_out,
       not_7_out, not_8_out, not_9_out, not_10_out, not_11_out, not_12_out, or_7_out;

  not not_1 (not_1_out, Funct[2]);
  not not_2 (not_2_out, Funct[3]);
  not not_3 (not_3_out, Funct[4]);
  not not_4 (not_4_out, Funct[5]);
  not not_5 (not_5_out, Opcode[4]);
  not not_6 (not_6_out, Opcode[5]);
  not not_7 (not_7_out, Funct[0]);
  not not_8 (not_8_out, Funct[1]);
  not not_9 (not_9_out, Opcode[0]);
  not not_10 (not_10_out, Opcode[1]);
  not not_11 (not_11_out, Opcode[2]);
  not not_12 (not_12_out, Opcode[3]);
  nor nor_1 (Use_Register_Destination, Opcode[5], Opcode[4], Opcode[3], Opcode[2], Opcode[1], Opcode[0]);
  and and_1 (and_1_out, Use_Register_Destination, Funct[0], Funct[5]);
  and and_2 (and_2_out, Opcode[0], Opcode[3], not_6_out);
  and and_3 (and_3_out, Use_Register_Destination, Funct[1], not_4_out);
  and and_4 (and_4_out, Use_Register_Destination, not_1_out, not_2_out, Funct[5]);
  and and_5 (and_5_out, not_10_out, not_11_out, Opcode[3]);
  and and_6 (and_6_out, Use_Register_Destination, Funct[0], not_4_out);
  and and_7 (and_7_out, Use_Register_Destination, Funct[1], Funct[5]);
  and and_8 (and_8_out, Opcode[1], not_11_out, not_6_out);
  and and_9 (and_9_out, not_9_out, Opcode[1], Opcode[2]);
  and and_10 (and_10_out, Use_Register_Destination, not_4_out);
  and and_11 (and_11_out, Use_Register_Destination, Funct[1], Funct[2]);
  and and_12 (and_12_out, not_9_out, Opcode[1], Opcode[2]);
  and and_13 (Use_MD, Use_Register_Destination, Funct[3], Funct[4]);
  and and_14 (Move_From_Low_High[1], Use_Register_Destination, not_2_out, Funct[4]);
  and and_15 (Memory_Write, Opcode[3], Opcode[5]);
  and and_16 (Jump, Opcode[1], not_12_out, not_6_out);
  and and_17 (Branch, Opcode[2], not_12_out);
  and and_18 (ALU_Source__Reg_Shamt_Imm[0], Use_Register_Destination, not_3_out, not_4_out);
  and and_19 (and_19_out, Use_Register_Destination, Funct[2], not_4_out);
  or or_1 (Signed_Immediate, not_11_out, not_12_out);
  and and_20 (and_20_out, Use_Register_Destination, not_2_out);
  and and_21 (and_21_out, Use_Register_Destination, Funct[5]);
  and and_22 (and_22_out, Opcode[3], not_6_out);
  and and_23 (and_23_out, not_12_out, Opcode[5]);
  and and_24 (and_24_out, Opcode[0], not_11_out, not_12_out);
  and and_25 (Jump_Register, Use_Register_Destination, Funct[3], not_3_out, not_4_out);
  and and_26 (and_26_out, Use_Register_Destination, Funct[3], Funct[0]);
  and and_27 (and_27_out, Opcode[2], Opcode[1], Opcode[0]);
  or or_2 (ALU_Control_Bits[0], and_1_out, and_2_out);
  or or_3 (ALU_Control_Bits[1], and_27_out, and_3_out, and_4_out, and_5_out, Opcode[5]);
  or or_4 (ALU_Control_Bits[2], and_27_out, and_6_out, and_7_out, and_8_out, and_9_out);
  or or_5 (ALU_Control_Bits[3], and_27_out, and_10_out, and_11_out, and_12_out);
  and and_28 (Move_From_Low_High[0], not_8_out, Move_From_Low_High[1]);
  or or_6 (ALU_Source__Reg_Shamt_Imm[1], Opcode[3], Opcode[5], and_19_out);
  or or_7 (or_7_out, and_20_out, and_21_out, and_22_out, and_23_out, and_24_out);
  // OR_Gate or_8: pin names not known; wires that end beside it: or_7_out, or_7_out, and_26_out, Register_Write

  assign Branch_Not_Equal = Opcode[0];
  assign MD_Control_Bits = Funct[1:0];
  assign Memory_Read = Opcode[5];
endmodule

module ALU__32_bit (
  input  [3:0] Control,
  input  [31:0] Input_1,
  input  [31:0] Input_2,
  output [31:0] Output,
  output Overflow
);

  wire and_3_out, and_12_out, and_13_out, bit_extender_2_p1, bit_extender_3_p2, bit_extender_4_p2,
       bit_extender_6_p1, eq_4_bit_1_p3, eq_4_bit_2_p1, eq_4_bit_3_p1, eq_4_bit_4_p1, eq_4_bit_5_p4,
       eq_4_bit_7_p3, eq_4_bit_8_p3, eq_4_bit_8_p4, eq_4_bit_9_p1, eq_4_bit_9_p4, eq_4_bit_10_p3,
       eq_4_bit_10_p4, eq_4_bit_11_p3, eq_4_bit_11_p4, eq_4_bit_12_p3, eq_4_bit_13_p6,
       eq_lt_signed_32_bit_1_p3, eq_lt_unsigned_32_bit_1_p3, not_1_out, not_2_out, not_3_out, or_2_out,
       or_4_out, or_15_out;
  wire [15:0] and_10_out, bit_extender_7_out;
  wire [31:0] add_32_1_out_4, and_1_out, and_4_out, and_5_out, and_6_out, and_7_out, and_8_out, and_9_out,
       and_11_out, bit_extender_1_out, bit_extender_2_p3, bit_extender_3_p4, bit_extender_4_p4,
       bit_extender_5_out, bit_extender_6_p3, bit_extender_8_out, bit_extender_9_p2, bit_extender_11_out,
       eq_4_bit_11_p5, nor_1_out, or_1_out, or_6_out, or_7_out, or_8_out, or_9_out, or_10_out, or_11_out,
       or_12_out, or_13_out, shiftl_variable_32_bit_1_p3, shiftr_variable_32_bit_1_p4, xor_1_out, xor_2_out;

  // eq__4_bit eq_4_bit_1: pin names not known; wires that end beside it: 4'b0000, Control, eq_4_bit_1_p3, eq_4_bit_1_p3
  assign and_1_out = Input_1 & Input_2;  // AND_Gate and_1, 32 bits wide
  // eq__4_bit eq_4_bit_2: pin names not known; wires that end beside it: eq_4_bit_2_p1, 4'b0001, eq_4_bit_2_p1
  assign or_1_out = Input_1 | Input_2;  // OR_Gate or_1, 32 bits wide
  // eq__4_bit eq_4_bit_3: pin names not known; wires that end beside it: eq_4_bit_3_p1, 4'b1101, eq_4_bit_3_p1
  assign nor_1_out = ~(Input_1 | Input_2);  // NOR_Gate nor_1, 32 bits wide
  // eq__4_bit eq_4_bit_4: pin names not known; wires that end beside it: eq_4_bit_4_p1, 4'b1100, eq_4_bit_4_p1, Input_2
  assign xor_1_out = Input_1 ^ Input_2;  // XOR_Gate xor_1, 32 bits wide
  // eq__4_bit eq_4_bit_5: pin names not known; wires that end beside it: 4'b1000, Control, Input_2, eq_4_bit_5_p4, eq_4_bit_5_p4
  // eq__4_bit eq_4_bit_6: pin names not known; wires that end beside it: 4'b1010, Control
  // eq__4_bit eq_4_bit_7: pin names not known; wires that end beside it: 4'b1111, Control, eq_4_bit_7_p3, eq_4_bit_7_p3
  // eq__4_bit eq_4_bit_8: pin names not known; wires that end beside it: 4'b0100, Control, eq_4_bit_8_p3, eq_4_bit_8_p4
  // eq_lt_signed__32_bit eq_lt_signed_32_bit_1: pin names not known; wires that end beside it: Input_1, Input_2, eq_lt_signed_32_bit_1_p3
  // eq__4_bit eq_4_bit_9: pin names not known; wires that end beside it: eq_4_bit_9_p1, 4'b0101, eq_4_bit_9_p1, eq_4_bit_9_p4
  // eq_lt_unsigned__32_bit eq_lt_unsigned_32_bit_1: pin names not known; wires that end beside it: Input_1, Input_2, eq_lt_unsigned_32_bit_1_p3
  // eq__4_bit eq_4_bit_10: pin names not known; wires that end beside it: 4'b0011, Control, eq_4_bit_10_p3, eq_4_bit_10_p4
  // eq__4_bit eq_4_bit_11: pin names not known; wires that end beside it: 4'b0111, Control, eq_4_bit_11_p3, eq_4_bit_11_p4, eq_4_bit_11_p5, Input_2
  // eq__4_bit eq_4_bit_12: pin names not known; wires that end beside it: 4'b0010, Control, eq_4_bit_12_p3
  // eq__4_bit eq_4_bit_13: pin names not known; wires that end beside it: Input_2, Input_1, Control, 4'b0110, Control, eq_4_bit_13_p6
  assign bit_extender_1_out = {{31{eq_4_bit_1_p3}}, eq_4_bit_1_p3};  // Bit_Extender bit_extender_1
  // Bit_Extender #(.in_width(1), .out_width(32), .\type ("sign")) bit_extender_2: pin names not known; wires that end beside it: bit_extender_2_p1, bit_extender_2_p1, bit_extender_2_p3
  // Bit_Extender #(.in_width(1), .out_width(32), .\type ("sign")) bit_extender_3: pin names not known; wires that end beside it: Input_1, bit_extender_3_p2, bit_extender_3_p2, bit_extender_3_p4
  // Bit_Extender #(.in_width(1), .out_width(32), .\type ("sign")) bit_extender_4: pin names not known; wires that end beside it: Input_1, bit_extender_4_p2, bit_extender_4_p2, bit_extender_4_p4
  assign bit_extender_5_out = {{31{eq_4_bit_5_p4}}, eq_4_bit_5_p4};  // Bit_Extender bit_extender_5
  // shiftl_variable__32_bit shiftl_variable_32_bit_1: pin names not known; wires that end beside it: Input_1, Input_2[4:0], shiftl_variable_32_bit_1_p3
  // Bit_Extender #(.in_width(1), .out_width(32), .\type ("sign")) bit_extender_6: pin names not known; wires that end beside it: bit_extender_6_p1, bit_extender_6_p1, bit_extender_6_p3
  // shiftr_variable__32_bit shiftr_variable_32_bit_1: pin names not known; wires that end beside it: Input_1, Input_2[4:0], 1'b0, shiftr_variable_32_bit_1_p4
  assign bit_extender_7_out = {{15{eq_4_bit_7_p3}}, eq_4_bit_7_p3};  // Bit_Extender bit_extender_7
  and and_2 (eq_4_bit_8_p4, eq_4_bit_8_p3, eq_lt_signed_32_bit_1_p3);
  and and_3 (and_3_out, eq_4_bit_9_p4, eq_lt_unsigned_32_bit_1_p3);
  or or_2 (or_2_out, eq_4_bit_10_p3, eq_4_bit_11_p3);
  or or_3 (eq_4_bit_11_p4, eq_4_bit_11_p3, eq_4_bit_13_p6);
  or or_4 (or_4_out, eq_4_bit_12_p3, eq_4_bit_13_p6);
  assign and_4_out = bit_extender_1_out & and_1_out;  // AND_Gate and_4, 32 bits wide
  assign and_5_out = bit_extender_2_p3 & or_1_out;  // AND_Gate and_5, 32 bits wide
  assign and_6_out = bit_extender_3_p4 & nor_1_out;  // AND_Gate and_6, 32 bits wide
  assign and_7_out = bit_extender_4_p4 & xor_1_out;  // AND_Gate and_7, 32 bits wide
  assign and_8_out = bit_extender_5_out & shiftl_variable_32_bit_1_p3;  // AND_Gate and_8, 32 bits wide
  assign and_9_out = bit_extender_6_p3 & shiftr_variable_32_bit_1_p4;  // AND_Gate and_9, 32 bits wide
  assign and_10_out = bit_extender_7_out & Input_2[15:0];  // AND_Gate and_10, 16 bits wide
  assign bit_extender_8_out = {{31{1'b0}}, eq_4_bit_8_p4};  // Bit_Extender bit_extender_8
  // Bit_Extender #(.in_width(1), .out_width(32)) bit_extender_9: pin names not known; wires that end beside it: and_3_out, bit_extender_9_p2
  or or_5 (eq_4_bit_10_p4, or_2_out, or_4_out);
  assign eq_4_bit_11_p5 = {{31{eq_4_bit_11_p4}}, eq_4_bit_11_p4};  // Bit_Extender bit_extender_10
  assign or_6_out = and_4_out | and_5_out;  // OR_Gate or_6, 32 bits wide
  assign or_7_out = or_6_out | or_8_out;  // OR_Gate or_7, 32 bits wide
  assign or_8_out = and_6_out | and_7_out;  // OR_Gate or_8, 32 bits wide
  assign or_9_out = and_8_out | and_9_out;  // OR_Gate or_9, 32 bits wide
  assign or_10_out = bit_extender_8_out | bit_extender_9_p2;  // OR_Gate or_10, 32 bits wide
  assign bit_extender_11_out = {{31{eq_4_bit_10_p4}}, eq_4_bit_10_p4};  // Bit_Extender bit_extender_11
  assign xor_2_out = eq_4_bit_11_p5 ^ Input_2;  // XOR_Gate xor_2, 32 bits wide
  add_32 add_32_1 (
    .in_1(Input_1), .in_2(xor_2_out), .out_4(add_32_1_out_4), .in_3(eq_4_bit_11_p4));  // open: out_5, out_6
  assign or_11_out = or_7_out | or_9_out;  // OR_Gate or_11, 32 bits wide
  assign or_12_out = {and_10_out, {16{1'b0}}} | or_10_out;  // OR_Gate or_12, 32 bits wide
  assign and_11_out = bit_extender_11_out & add_32_1_out_4;  // AND_Gate and_11, 32 bits wide
  not not_1 (not_1_out, xor_2_out[31]);
  not not_2 (not_2_out, Input_1[31]);
  not not_3 (not_3_out, add_32_1_out_4[31]);
  assign or_13_out = or_11_out | or_12_out;  // OR_Gate or_13, 32 bits wide
  assign Output = or_13_out | and_11_out;  // OR_Gate or_14, 32 bits wide
  and and_12 (and_12_out, not_1_out, add_32_1_out_4[31], not_2_out);
  or or_15 (or_15_out, and_12_out, and_13_out);
  and and_13 (and_13_out, xor_2_out[31], not_3_out, Input_1[31]);
  and and_14 (Overflow, or_15_out, or_4_out);
endmodule

module MD__32_bit (
  input  [1:0] Control,
  input  [31:0] Input_1,
  input  [31:0] Input_2,
  output [31:0] Output_Low_Bits,
  output [31:0] Output_High_Bits
);

  wire xor_1_out;
  wire [31:0] adder_1_out, adder_2_out, and_1_out, and_2_out, bit_extender_1_out, bit_extender_2_out,
       divider_1_out, divider_1_rem, divider_2_out, divider_2_rem, multiplexer_1_out, multiplexer_2_out,
       multiplexer_3_out, multiplier_1_cout, multiplier_1_out, negator_1_out, negator_2_out, negator_3_out;

  Negator #(.width(32)) negator_1 (.in(Input_1), .out(negator_1_out));
  Negator #(.width(32)) negator_2 (.in(Input_2), .out(negator_2_out));
  assign and_1_out = Input_2 & bit_extender_1_out;  // AND_Gate and_1, 32 bits wide
  assign bit_extender_1_out = {{31{Input_1[31]}}, Input_1[31]};  // Bit_Extender bit_extender_1
  assign and_2_out = Input_1 & bit_extender_2_out;  // AND_Gate and_2, 32 bits wide
  assign bit_extender_2_out = {{31{Input_2[31]}}, Input_2[31]};  // Bit_Extender bit_extender_2
  Multiplexer #(.width(32), .enable("false")) multiplexer_1 (
    .in0(Input_1), .in1(negator_1_out), .out(multiplexer_1_out), .sel(Input_1[31]));
  Multiplexer #(.width(32), .enable("false")) multiplexer_2 (
    .in0(Input_2), .in1(negator_2_out), .out(multiplexer_2_out), .sel(Input_2[31]));
  Multiplier #(.width(32)) multiplier_1 (
    .a(Input_1), .b(Input_2), .out(multiplier_1_out), .cout(multiplier_1_cout));  // open: cin
  Adder #(.width(32)) adder_1 (.a(and_1_out), .b(and_2_out), .out(adder_1_out));  // open: cin, cout
  Divider #(.width(32)) divider_1 (
    .a(multiplexer_1_out), .b(multiplexer_2_out), .out(divider_1_out), .rem(divider_1_rem));  // open: upper
  Negator #(.width(32)) negator_3 (.in(divider_1_out), .out(negator_3_out));
  Divider #(.width(32)) divider_2 (.a(Input_1), .b(Input_2), .out(divider_2_out), .rem(divider_2_rem));  // open: upper
  Adder #(.width(32)) adder_2 (.a(multiplier_1_cout), .b(adder_1_out), .out(adder_2_out));  // open: cin, cout
  xor xor_1 (xor_1_out, Input_1[31], Input_2[31]);
  Multiplexer #(.width(32), .enable("false")) multiplexer_3 (
    .in0(divider_1_out), .in1(negator_3_out), .out(multiplexer_3_out), .sel(xor_1_out));
  Multiplexer #(.select(2), .width(32), .enable("false")) multiplexer_4 (
    .in0(multiplier_1_out), .in1(multiplier_1_out), .in2(multiplexer_3_out), .in3(divider_2_out),
    .out(Output_Low_Bits), .sel(Control));
  Multiplexer #(.select(2), .width(32), .enable("false")) multiplexer_5 (
    .in0(multiplier_1_cout), .in1(adder_2_out), .in2(divider_1_rem), .in3(divider_2_rem),
    .out(Output_High_Bits), .sel(Control));
endmodule

module register__32_bit (
  input  Write,
  input  [31:0] Input,
  input  Clock,
  output [31:0] Output
);

  D_Flip_Flop d_ff_1 (.clk(Clock), .D(Input[0]), .Q(Output[0]), .en(Write));  // open: Qn, preset, reset
  D_Flip_Flop d_ff_2 (.clk(Clock), .D(Input[1]), .Q(Output[1]), .en(Write));  // open: Qn, preset, reset
  D_Flip_Flop d_ff_3 (.clk(Clock), .D(Input[2]), .Q(Output[2]), .en(Write));  // open: Qn, preset, reset
  D_Flip_Flop d_ff_4 (.clk(Clock), .D(Input[3]), .Q(Output[3]), .en(Write));  // open: Qn, preset, reset
  D_Flip_Flop d_ff_5 (.clk(Clock), .D(Input[4]), .Q(Output[4]), .en(Write));  // open: Qn, preset, reset
  D_Flip_Flop d_ff_6 (.clk(Clock), .D(Input[5]), .Q(Output[5]), .en(Write));  // open: Qn, preset, reset
  D_Flip_Flop d_ff_7 (.clk(Clock), .D(Input[6]), .Q(Output[6]), .en(Write));  // open: Qn, preset, reset
  D_Flip_Flop d_ff_8 (.clk(Clock), .D(Input[7]), .Q(Output[7]), .en(Write));  // open: Qn, preset, reset
  D_Flip_Flop d_ff_9 (.clk(Clock), .D(Input[8]), .Q(Output[8]), .en(Write));  // open: Qn, preset, reset
  D_Flip_Flop d_ff_10 (.clk(Clock), .D(Input[9]), .Q(Output[9]), .en(Write));  // open: Qn, preset, reset
  D_Flip_Flop d_ff_11 (.clk(Clock), .D(Input[10]), .Q(Output[10]), .en(Write));  // open: Qn, preset, reset
  D_Flip_Flop d_ff_12 (.clk(Clock), .D(Input[11]), .Q(Output[11]), .en(Write));  // open: Qn, preset, reset
  D_Flip_Flop d_ff_13 (.clk(Clock), .D(Input[12]), .Q(Output[12]), .en(Write));  // open: Qn, preset, reset
  D_Flip_Flop d_ff_14 (.clk(Clock), .D(Input[13]), .Q(Output[13]), .en(Write));  // open: Qn, preset, reset
  D_Flip_Flop d_ff_15 (.clk(Clock), .D(Input[14]), .Q(Output[14]), .en(Write));  // open: Qn, preset, reset
  D_Flip_Flop d_ff_16 (.clk(Clock), .D(Input[15]), .Q(Output[15]), .en(Write));  // open: Qn, preset, reset
  D_Flip_Flop d_ff_17 (.clk(Clock), .D(Input[16]), .Q(Output[16]), .en(Write));  // open: Qn, preset, reset
  D_Flip_Flop d_ff_18 (.clk(Clock), .D(Input[17]), .Q(Output[17]), .en(Write));  // open: Qn, preset, reset
  D_Flip_Flop d_ff_19 (.clk(Clock), .D(Input[18]), .Q(Output[18]), .en(Write));  // open: Qn, preset, reset
  D_Flip_Flop d_ff_20 (.clk(Clock), .D(Input[19]), .Q(Output[19]), .en(Write));  // open: Qn, preset, reset
  D_Flip_Flop d_ff_21 (.clk(Clock), .D(Input[20]), .Q(Output[20]), .en(Write));  // open: Qn, preset, reset
  D_Flip_Flop d_ff_22 (.clk(Clock), .D(Input[21]), .Q(Output[21]), .en(Write));  // open: Qn, preset, reset
  D_Flip_Flop d_ff_23 (.clk(Clock), .D(Input[22]), .Q(Output[22]), .en(Write));  // open: Qn, preset, reset
  D_Flip_Flop d_ff_24 (.clk(Clock), .D(Input[23]), .Q(Output[23]), .en(Write));  // open: Qn, preset, reset
  D_Flip_Flop d_ff_25 (.clk(Clock), .D(Input[24]), .Q(Output[24]), .en(Write));  // open: Qn, preset, reset
  D_Flip_Flop d_ff_26 (.clk(Clock), .D(Input[25]), .Q(Output[25]), .en(Write));  // open: Qn, preset, reset
  D_Flip_Flop d_ff_27 (.clk(Clock), .D(Input[26]), .Q(Output[26]), .en(Write));  // open: Qn, preset, reset
  D_Flip_Flop d_ff_28 (.clk(Clock), .D(Input[27]), .Q(Output[27]), .en(Write));  // open: Qn, preset, reset
  D_Flip_Flop d_ff_29 (.clk(Clock), .D(Input[28]), .Q(Output[28]), .en(Write));  // open: Qn, preset, reset
  D_Flip_Flop d_ff_30 (.clk(Clock), .D(Input[29]), .Q(Output[29]), .en(Write));  // open: Qn, preset, reset
  D_Flip_Flop d_ff_31 (.clk(Clock), .D(Input[30]), .Q(Output[30]), .en(Write));  // open: Qn, preset, reset
  D_Flip_Flop d_ff_32 (.clk(Clock), .D(Input[31]), .Q(Output[31]), .en(Write));  // open: Qn, preset, reset
endmodule

module register_file__32_bit (
  input  Write,
  input  [4:0] Write_Register,
  input  [4:0] Read_Register_1,
  input  [4:0] Read_Register_2,
  input  [31:0] Input,
  input  Clock,
  output [31:0] Output_1,
  output [31:0] Output_2
);

  wire decoder_1_out0, decoder_1_out1, decoder_1_out2, decoder_1_out3, decoder_1_out4, decoder_1_out5,
       decoder_1_out6, decoder_1_out7, decoder_1_out8, decoder_1_out9, decoder_1_out10, decoder_1_out11,
       decoder_1_out12, decoder_1_out13, decoder_1_out14, decoder_1_out15, decoder_1_out16, decoder_1_out17,
       decoder_1_out18, decoder_1_out19, decoder_1_out20, decoder_1_out21, decoder_1_out22, decoder_1_out23,
       decoder_1_out24, decoder_1_out25, decoder_1_out26, decoder_1_out27, decoder_1_out28, decoder_1_out29,
       decoder_1_out30, decoder_1_out31;
  wire [31:0] register_32_bit_1_output, register_32_bit_2_output, register_32_bit_3_output,
       register_32_bit_4_output, register_32_bit_5_output, register_32_bit_6_output,
       register_32_bit_7_output, register_32_bit_8_output, register_32_bit_9_output,
       register_32_bit_10_output, register_32_bit_11_output, register_32_bit_12_output,
       register_32_bit_13_output, register_32_bit_14_output, register_32_bit_15_output,
       register_32_bit_16_output, register_32_bit_17_output, register_32_bit_18_output,
       register_32_bit_19_output, register_32_bit_20_output, register_32_bit_21_output,
       register_32_bit_22_output, register_32_bit_23_output, register_32_bit_24_output,
       register_32_bit_25_output, register_32_bit_26_output, register_32_bit_27_output,
       register_32_bit_28_output, register_32_bit_29_output, register_32_bit_30_output,
       register_32_bit_31_output, register_32_bit_32_output;

  Decoder #(.select(5), .disabled(0)) decoder_1 (
    .out0(decoder_1_out0), .out1(decoder_1_out1), .out2(decoder_1_out2), .out3(decoder_1_out3),
    .out4(decoder_1_out4), .out5(decoder_1_out5), .out6(decoder_1_out6), .out7(decoder_1_out7),
    .out8(decoder_1_out8), .out9(decoder_1_out9), .out10(decoder_1_out10), .out11(decoder_1_out11),
    .out12(decoder_1_out12), .out13(decoder_1_out13), .out14(decoder_1_out14), .out15(decoder_1_out15),
    .out16(decoder_1_out16), .out17(decoder_1_out17), .out18(decoder_1_out18), .out19(decoder_1_out19),
    .out20(decoder_1_out20), .out21(decoder_1_out21), .out22(decoder_1_out22), .out23(decoder_1_out23),
    .out24(decoder_1_out24), .out25(decoder_1_out25), .out26(decoder_1_out26), .out27(decoder_1_out27),
    .out28(decoder_1_out28), .out29(decoder_1_out29), .out30(decoder_1_out30), .out31(decoder_1_out31),
    .sel(Write_Register), .en(Write));
  register__32_bit register_32_bit_1 (
    .Input(Input), .Write(decoder_1_out31), .Clock(Clock), .Output(register_32_bit_1_output));
  register__32_bit register_32_bit_2 (
    .Input(Input), .Write(decoder_1_out30), .Clock(Clock), .Output(register_32_bit_2_output));
  register__32_bit register_32_bit_3 (
    .Input(Input), .Write(decoder_1_out29), .Clock(Clock), .Output(register_32_bit_3_output));
  register__32_bit register_32_bit_4 (
    .Input(Input), .Write(decoder_1_out28), .Clock(Clock), .Output(register_32_bit_4_output));
  register__32_bit register_32_bit_5 (
    .Input(Input), .Write(decoder_1_out27), .Clock(Clock), .Output(register_32_bit_5_output));
  register__32_bit register_32_bit_6 (
    .Input(Input), .Write(decoder_1_out26), .Clock(Clock), .Output(register_32_bit_6_output));
  register__32_bit register_32_bit_7 (
    .Input(Input), .Write(decoder_1_out25), .Clock(Clock), .Output(register_32_bit_7_output));
  register__32_bit register_32_bit_8 (
    .Input(Input), .Write(decoder_1_out24), .Clock(Clock), .Output(register_32_bit_8_output));
  register__32_bit register_32_bit_9 (
    .Input(Input), .Write(decoder_1_out23), .Clock(Clock), .Output(register_32_bit_9_output));
  register__32_bit register_32_bit_10 (
    .Input(Input), .Write(decoder_1_out22), .Clock(Clock), .Output(register_32_bit_10_output));
  register__32_bit register_32_bit_11 (
    .Input(Input), .Write(decoder_1_out21), .Clock(Clock), .Output(register_32_bit_11_output));
  register__32_bit register_32_bit_12 (
    .Input(Input), .Write(decoder_1_out20), .Clock(Clock), .Output(register_32_bit_12_output));
  register__32_bit register_32_bit_13 (
    .Input(Input), .Write(decoder_1_out19), .Clock(Clock), .Output(register_32_bit_13_output));
  register__32_bit register_32_bit_14 (
    .Input(Input), .Write(decoder_1_out18), .Clock(Clock), .Output(register_32_bit_14_output));
  register__32_bit register_32_bit_15 (
    .Input(Input), .Write(decoder_1_out17), .Clock(Clock), .Output(register_32_bit_15_output));
  register__32_bit register_32_bit_16 (
    .Input(Input), .Write(decoder_1_out16), .Clock(Clock), .Output(register_32_bit_16_output));
  register__32_bit register_32_bit_17 (
    .Input(Input), .Write(decoder_1_out15), .Clock(Clock), .Output(register_32_bit_17_output));
  register__32_bit register_32_bit_18 (
    .Input(Input), .Write(decoder_1_out14), .Clock(Clock), .Output(register_32_bit_18_output));
  register__32_bit register_32_bit_19 (
    .Input(Input), .Write(decoder_1_out13), .Clock(Clock), .Output(register_32_bit_19_output));
  register__32_bit register_32_bit_20 (
    .Input(Input), .Write(decoder_1_out12), .Clock(Clock), .Output(register_32_bit_20_output));
  register__32_bit register_32_bit_21 (
    .Input(Input), .Write(decoder_1_out11), .Clock(Clock), .Output(register_32_bit_21_output));
  register__32_bit register_32_bit_22 (
    .Input(Input), .Write(decoder_1_out10), .Clock(Clock), .Output(register_32_bit_22_output));
  register__32_bit register_32_bit_23 (
    .Input(Input), .Write(decoder_1_out9), .Clock(Clock), .Output(register_32_bit_23_output));
  register__32_bit register_32_bit_24 (
    .Input(Input), .Write(decoder_1_out8), .Clock(Clock), .Output(register_32_bit_24_output));
  register__32_bit register_32_bit_25 (
    .Input(Input), .Write(decoder_1_out7), .Clock(Clock), .Output(register_32_bit_25_output));
  register__32_bit register_32_bit_26 (
    .Input(Input), .Write(decoder_1_out6), .Clock(Clock), .Output(register_32_bit_26_output));
  register__32_bit register_32_bit_27 (
    .Input(Input), .Write(decoder_1_out5), .Clock(Clock), .Output(register_32_bit_27_output));
  register__32_bit register_32_bit_28 (
    .Input(Input), .Write(decoder_1_out4), .Clock(Clock), .Output(register_32_bit_28_output));
  register__32_bit register_32_bit_29 (
    .Input(Input), .Write(decoder_1_out3), .Clock(Clock), .Output(register_32_bit_29_output));
  register__32_bit register_32_bit_30 (
    .Input(Input), .Write(decoder_1_out2), .Clock(Clock), .Output(register_32_bit_30_output));
  register__32_bit register_32_bit_31 (
    .Input(Input), .Write(decoder_1_out1), .Clock(Clock), .Output(register_32_bit_31_output));
  register__32_bit register_32_bit_32 (
    .Input(Input), .Write(decoder_1_out0), .Clock(Clock), .Output(register_32_bit_32_output));
  Multiplexer #(.select(5), .width(32), .enable("false")) multiplexer_1 (
    .in0(register_32_bit_32_output), .in1(register_32_bit_31_output), .in2(register_32_bit_30_output),
    .in3(register_32_bit_29_output), .in4(register_32_bit_28_output), .in5(register_32_bit_27_output),
    .in6(register_32_bit_26_output), .in7(register_32_bit_25_output), .in8(register_32_bit_24_output),
    .in9(register_32_bit_23_output), .in10(register_32_bit_22_output), .in11(register_32_bit_21_output),
    .in12(register_32_bit_20_output), .in13(register_32_bit_19_output), .in14(register_32_bit_18_output),
    .in15(register_32_bit_17_output), .in16(register_32_bit_16_output), .in17(register_32_bit_15_output),
    .in18(register_32_bit_14_output), .in19(register_32_bit_13_output), .in20(register_32_bit_12_output),
    .in21(register_32_bit_11_output), .in22(register_32_bit_10_output), .in23(register_32_bit_9_output),
    .in24(register_32_bit_8_output), .in25(register_32_bit_7_output), .in26(register_32_bit_6_output),
    .in27(register_32_bit_5_output), .in28(register_32_bit_4_output), .in29(register_32_bit_3_output),
    .in30(register_32_bit_2_output), .in31(register_32_bit_1_output), .out(Output_1), .sel(Read_Register_1));
  Multiplexer #(.select(5), .width(32), .enable("false")) multiplexer_2 (
    .in0(register_32_bit_32_output), .in1(register_32_bit_31_output), .in2(register_32_bit_30_output),
    .in3(register_32_bit_29_output), .in4(register_32_bit_28_output), .in5(register_32_bit_27_output),
    .in6(register_32_bit_26_output), .in7(register_32_bit_25_output), .in8(register_32_bit_24_output),
    .in9(register_32_bit_23_output), .in10(register_32_bit_22_output), .in11(register_32_bit_21_output),
    .in12(register_32_bit_20_output), .in13(register_32_bit_19_output), .in14(register_32_bit_18_output),
    .in15(register_32_bit_17_output), .in16(register_32_bit_16_output), .in17(register_32_bit_15_output),
    .in18(register_32_bit_14_output), .in19(register_32_bit_13_output), .in20(register_32_bit_12_output),
    .in21(register_32_bit_11_output), .in22(register_32_bit_10_output), .in23(register_32_bit_9_output),
    .in24(register_32_bit_8_output), .in25(register_32_bit_7_output), .in26(register_32_bit_6_output),
    .in27(register_32_bit_5_output), .in28(register_32_bit_4_output), .in29(register_32_bit_3_output),
    .in30(register_32_bit_2_output), .in31(register_32_bit_1_output), .out(Output_2), .sel(Read_Register_2));
endmodule

module program_counter_interface__32_bit (
  input  [31:0] Input,
  input  [31:0] Set_Value,
  input  Set,
  input  Clock,
  output [31:0] out_5
);

  wire and_1_out, delay_4_gates_1_out_2, not_1_out, xor_1_out;
  wire [31:0] multiplexer_1_out;

  delay__4_gates delay_4_gates_1 (.in_1(Set), .out_2(delay_4_gates_1_out_2));
  Multiplexer #(.width(32), .enable("false")) multiplexer_1 (
    .in0(Input), .in1(Set_Value), .out(multiplexer_1_out), .sel(Set));
  and and_1 (and_1_out, delay_4_gates_1_out_2, not_1_out);
  not not_1 (not_1_out, delay_4_gates_1_out_2);
  register__32_bit register_32_bit_1 (.Input(multiplexer_1_out), .Write(1'b1), .Clock(xor_1_out), .Output(out_5));
  xor xor_1 (xor_1_out, and_1_out, Clock);
endmodule

module delay__4_gates (
  input  in_1,
  output out_2
);

  wire not_1_out, not_2_out, not_3_out;

  not not_1 (not_1_out, in_1);
  not not_2 (not_2_out, not_3_out);
  not not_3 (not_3_out, not_1_out);
  not not_4 (out_2, not_2_out);
endmodule
